// Logisim project Problem_1_b.circ as structural Verilog: 1 circuit, main circuit main
module main (
);

  wire A_out, and_1_out, B_out, C_out, D_out, not_1_out, or_1_out;

  Button A (.out(A_out));
  Button B (.out(B_out));
  Button C (.out(C_out));
  Button D (.out(D_out));
  not not_1 (not_1_out, D_out);
  or or_1 (or_1_out, A_out, not_1_out);
  and and_1 (and_1_out, B_out, C_out, or_1_out);
endmodule
