// Logisim project Problem_5.circ as structural Verilog: 1 circuit, main circuit main
module main (
);

  wire and_1_out, and_2_out, and_3_out, and_4_out, not_1_out, not_2_out, not_3_out, not_4_out, or_1_out,
       or_2_out, W_out, X_out, Y_out, Z_out;

  Button W (.out(W_out));
  Button X (.out(X_out));
  Button Y (.out(Y_out));
  Button Z (.out(Z_out));
  not not_1 (not_1_out, W_out);
  not not_2 (not_2_out, X_out);
  not not_3 (not_3_out, Y_out);
  not not_4 (not_4_out, Z_out);
  and and_1 (and_1_out, not_1_out, not_2_out, not_3_out);
  and and_2 (and_2_out, W_out, not_3_out, not_4_out);
  and and_3 (and_3_out, not_1_out, not_3_out, not_4_out);
  or or_1 (or_1_out, and_1_out, and_2_out, and_3_out);
  and and_4 (and_4_out, not_4_out, X_out);
  or or_2 (or_2_out, W_out, and_4_out);
  LED B (.in(or_1_out));
  LED A (.in(or_2_out));
endmodule
