// Logisim project Problem_6.circ as structural Verilog: 1 circuit, main circuit main
module main (
);

  wire A0_out, A1_out, CONTROL_out, nand_1_out, nand_2_out, nand_3_out, nand_4_out, nand_5_out, nand_6_out,
       nand_7_out, nand_8_out;

  Button CONTROL (.out(CONTROL_out));
  Button A0 (.out(A0_out));
  Button A1 (.out(A1_out));
  nand nand_1 (nand_1_out, CONTROL_out, CONTROL_out);
  nand nand_2 (nand_2_out, nand_1_out, A0_out);
  nand nand_3 (nand_3_out, CONTROL_out, A1_out);
  nand nand_4 (nand_4_out, nand_2_out, nand_2_out);
  nand nand_5 (nand_5_out, nand_3_out, nand_3_out);
  nand nand_6 (nand_6_out, nand_4_out, nand_4_out);
  nand nand_7 (nand_7_out, nand_5_out, nand_5_out);
  nand nand_8 (nand_8_out, nand_6_out, nand_7_out);
  LED OUTPUT (.in(nand_8_out));
endmodule
