// Logisim project Problem_7.circ as structural Verilog: 1 circuit, main circuit main
module main (
  input  C_out,
  input  A,
  input  B
);

  wire and_1_out, and_2_out, or_1_out, xor_1_out, xor_2_out;

  and and_1 (and_1_out, A, B);
  xor xor_1 (xor_1_out, A, B);
  or or_1 (or_1_out, and_1_out, and_2_out);
  LED u_C_out ();  // open: in
  and and_2 (and_2_out, C_out, xor_1_out);
  LED OUTPUT (.in(xor_2_out));
  xor xor_2 (xor_2_out, C_out, xor_1_out);
endmodule
