// Logisim project P1_d.circ as structural Verilog: 1 circuit, main circuit main
module main (
  input  I_0,
  input  I_1
);

  wire and_1_out, and_2_out, and_3_out, and_4_out, and_5_out, and_6_out, and_7_out, and_8_out, and_9_out,
       clock_1_out, I_0_out, I_1_out, not_1_out, not_2_out, not_3_out, not_4_out, or_1_out, or_2_out,
       or_3_out, S0_q, S1_q;

  Clock clock_1 (.out(clock_1_out));
  Button u_I_0 (.out(I_0_out));
  Button u_I_1 (.out(I_1_out));
  D_Flip_Flop S0 (.clk(clock_1_out), .D(or_2_out), .Q(S0_q));  // open: Qn, preset, en, reset
  D_Flip_Flop S1 (.clk(clock_1_out), .D(or_1_out), .Q(S1_q));  // open: Qn, preset, en, reset
  not not_1 (not_1_out, S1_q);
  not not_2 (not_2_out, S0_q);
  and and_1 (and_1_out, I_0_out, not_1_out);
  and and_2 (and_2_out, I_1_out, not_1_out);
  and and_3 (and_3_out, I_0_out, I_1_out, S0_q);
  and and_4 (and_4_out, S0_q, not_1_out);
  and and_5 (and_5_out, not_2_out, S1_q);
  or or_1 (or_1_out, and_1_out, and_2_out, and_3_out, and_4_out);
  or or_2 (or_2_out, and_3_out, and_4_out, and_5_out);
  not not_3 (not_3_out, or_1_out);
  not not_4 (not_4_out, or_2_out);
  and and_6 (and_6_out, not_3_out, not_4_out);
  and and_7 (and_7_out, or_1_out, not_4_out);
  and and_8 (and_8_out, not_3_out, or_2_out);
  and and_9 (and_9_out, or_2_out, or_1_out);
  LED Green (.in(and_6_out));
  LED Red (.in(and_7_out));
  or or_3 (or_3_out, and_8_out, and_9_out);
  LED Red_2 (.in(or_3_out));

  // Notes on the sheet:
  //   Q1
  //   Q0
endmodule
