// Logisim project P2.circ as structural Verilog: 1 circuit, main circuit main
module main (
  input  In_Out_0,
  input  Selector,
  input  Loader,
  input  In_Out_1,
  input  ADD_0,
  input  ADD_1
);

  wire and_1_out, and_2_out, and_3_out, and_4_out, and_5_out, and_6_out, clock_1_out,
       controlled_buffer_1_out, controlled_buffer_2_out, controlled_buffer_3_out, controlled_buffer_5_out,
       d_ff_1_q, d_ff_2_q, d_ff_3_q, d_ff_4_q, d_ff_5_q, d_ff_6_q, d_ff_7_q, d_ff_8_q, decoder_1_out0,
       decoder_1_out1, decoder_1_out2, decoder_1_out3, multiplexer_1_out, multiplexer_2_out, not_1_out;

  D_Flip_Flop d_ff_1 (
    .clk(clock_1_out), .D(controlled_buffer_1_out), .Q(d_ff_1_q), .en(and_3_out));  // open: Qn, preset, reset
  not not_1 (not_1_out, Loader);
  Clock clock_1 (.out(clock_1_out));
  D_Flip_Flop d_ff_2 (
    .clk(clock_1_out), .D(controlled_buffer_1_out), .Q(d_ff_2_q), .en(and_4_out));  // open: Qn, preset, reset
  and and_1 (and_1_out, Selector, Loader);
  and and_2 (and_2_out, Selector, not_1_out);
  D_Flip_Flop d_ff_3 (
    .clk(clock_1_out), .D(controlled_buffer_1_out), .Q(d_ff_3_q), .en(and_5_out));  // open: Qn, preset, reset
  D_Flip_Flop d_ff_4 (
    .clk(clock_1_out), .D(controlled_buffer_1_out), .Q(d_ff_4_q), .en(and_6_out));  // open: Qn, preset, reset
  Decoder #(.select(2)) decoder_1 (
    .out0(decoder_1_out0), .out1(decoder_1_out1), .out2(decoder_1_out2), .out3(decoder_1_out3),
    .sel({ADD_1, ADD_0}));
  Multiplexer #(.select(2)) multiplexer_1 (
    .in0(d_ff_1_q), .in1(d_ff_2_q), .in2(d_ff_3_q), .in3(d_ff_4_q), .out(multiplexer_1_out),
    .sel({ADD_1, ADD_0}));
  and and_3 (and_3_out, and_2_out, decoder_1_out0);
  D_Flip_Flop d_ff_5 (
    .clk(clock_1_out), .D(controlled_buffer_2_out), .Q(d_ff_5_q), .en(and_3_out));  // open: Qn, preset, reset
  D_Flip_Flop d_ff_6 (
    .clk(clock_1_out), .D(controlled_buffer_2_out), .Q(d_ff_6_q), .en(and_4_out));  // open: Qn, preset, reset
  and and_4 (and_4_out, and_2_out, decoder_1_out1);
  D_Flip_Flop d_ff_7 (
    .clk(clock_1_out), .D(controlled_buffer_2_out), .Q(d_ff_7_q), .en(and_5_out));  // open: Qn, preset, reset
  and and_5 (and_5_out, and_2_out, decoder_1_out2);
  D_Flip_Flop d_ff_8 (
    .clk(clock_1_out), .D(controlled_buffer_2_out), .Q(d_ff_8_q), .en(and_6_out));  // open: Qn, preset, reset
  and and_6 (and_6_out, and_2_out, decoder_1_out3);
  assign controlled_buffer_1_out = and_1_out ? multiplexer_1_out : 1'bz;  // Controlled_Buffer controlled_buffer_1
  assign controlled_buffer_2_out = and_1_out ? multiplexer_2_out : 1'bz;  // Controlled_Buffer controlled_buffer_2
  Multiplexer #(.select(2)) multiplexer_2 (
    .in0(d_ff_5_q), .in1(d_ff_6_q), .in2(d_ff_7_q), .in3(d_ff_8_q), .out(multiplexer_2_out),
    .sel({ADD_1, ADD_0}));
  assign controlled_buffer_3_out = and_1_out ? controlled_buffer_1_out : 1'bz;  // Controlled_Buffer controlled_buffer_3
  assign controlled_buffer_1_out = and_2_out ? In_Out_0 : 1'bz;  // Controlled_Buffer controlled_buffer_4
  LED led_1 (.in(controlled_buffer_3_out));
  assign controlled_buffer_5_out = and_1_out ? controlled_buffer_2_out : 1'bz;  // Controlled_Buffer controlled_buffer_5
  LED led_2 (.in(controlled_buffer_5_out));
  assign controlled_buffer_2_out = and_2_out ? In_Out_1 : 1'bz;  // Controlled_Buffer controlled_buffer_6

  // Notes on the sheet:
  //   Input/Output_0
  //   Input/Output_1
  //   Testing purpose
endmodule
