// Logisim project RISC.circ as structural Verilog: 1 circuit, main circuit main
module main (
  input  Clear,
  input  CLEAR_2
);

  wire and_1_out, and_2_out, and_3_out, and_4_out, and_5_out, and_6_out, and_7_out, and_8_out, and_9_out,
       and_10_out, clock_1_out, decoder_1_out0, decoder_1_out1, decoder_1_out2, decoder_1_out3,
       decoder_1_out4, decoder_1_out5, decoder_1_out6, decoder_1_out7, not_2_out, or_1_out;
  wire [0:0] nor_1_out;
  wire [3:0] R0_q, R0_q_2, R0_q_3, R0_q_4, R1_q, R1_q_2, R1_q_3, R1_q_4, R3_q, R3_q_2, R3_q_3, R3_q_4, R4_q,
       R4_q_2, R5_q, R5_q_2;
  wire [15:0] adder_1_out, adder_2_out, adder_3_out, controlled_buffer_1_out, multiplexer_1_out,
       multiplexer_2_out, multiplexer_3_out, multiplexer_4_out, not_1_out, PC_q, R2_q, R6_q, R7_q,
       ram_1_data, rom_1_data, rom_2_data;
  wire [15:8] R4_q_3, R5_q_3, rom_1_data_2;

  Hex_Digit_Display hex_digit_display_1 (.value(R7_q[15:12]));  // open: dp
  Hex_Digit_Display hex_digit_display_2 (.value(R6_q[15:12]));  // open: dp
  Hex_Digit_Display hex_digit_display_3 (.value(R5_q_3[15:12]));  // open: dp
  Hex_Digit_Display hex_digit_display_4 (.value(R4_q_3[15:12]));  // open: dp
  Hex_Digit_Display hex_digit_display_5 (.value(R7_q[11:8]));  // open: dp
  Hex_Digit_Display hex_digit_display_6 (.value(R7_q[7:4]));  // open: dp
  Hex_Digit_Display hex_digit_display_7 (.value(R6_q[7:4]));  // open: dp
  Hex_Digit_Display hex_digit_display_8 (.value(R6_q[11:8]));  // open: dp
  Hex_Digit_Display hex_digit_display_9 (.value(R5_q_3[11:8]));  // open: dp
  Hex_Digit_Display hex_digit_display_10 (.value(R5_q_2));  // open: dp
  Hex_Digit_Display hex_digit_display_11 (.value(R4_q_3[11:8]));  // open: dp
  Hex_Digit_Display hex_digit_display_12 (.value(R4_q_2));  // open: dp
  Hex_Digit_Display hex_digit_display_13 (.value(R7_q[3:0]));  // open: dp
  Hex_Digit_Display hex_digit_display_14 (.value(R6_q[3:0]));  // open: dp
  Hex_Digit_Display hex_digit_display_15 (.value(R5_q));  // open: dp
  Hex_Digit_Display hex_digit_display_16 (.value(R4_q));  // open: dp
  Hex_Digit_Display hex_digit_display_17 (.value(R3_q_4));  // open: dp
  Hex_Digit_Display hex_digit_display_18 (.value(R2_q[15:12]));  // open: dp
  Hex_Digit_Display hex_digit_display_19 (.value(R1_q_4));  // open: dp
  Hex_Digit_Display hex_digit_display_20 (.value(R0_q_4));  // open: dp
  Hex_Digit_Display hex_digit_display_21 (.value(R3_q_2));  // open: dp
  Hex_Digit_Display hex_digit_display_22 (.value(R3_q_3));  // open: dp
  Hex_Digit_Display hex_digit_display_23 (.value(R2_q[11:8]));  // open: dp
  Hex_Digit_Display hex_digit_display_24 (.value(R1_q_3));  // open: dp
  Hex_Digit_Display hex_digit_display_25 (.value(R0_q_3));  // open: dp
  Hex_Digit_Display hex_digit_display_26 (.value(R3_q));  // open: dp
  Hex_Digit_Display hex_digit_display_27 (.value(R2_q[3:0]));  // open: dp
  Hex_Digit_Display hex_digit_display_28 (.value(R2_q[7:4]));  // open: dp
  Hex_Digit_Display hex_digit_display_29 (.value(R1_q_2));  // open: dp
  Hex_Digit_Display hex_digit_display_30 (.value(R1_q));  // open: dp
  Hex_Digit_Display hex_digit_display_31 (.value(R0_q_2));  // open: dp
  Hex_Digit_Display hex_digit_display_32 (.value(R0_q));  // open: dp
  Clock clock_1 (.out(clock_1_out));
  assign controlled_buffer_1_out = rom_2_data[3] ? multiplexer_1_out : 16'bz;  // Controlled_Buffer controlled_buffer_1
  assign controlled_buffer_1_out = rom_2_data[6] ? multiplexer_3_out : 16'bz;  // Controlled_Buffer controlled_buffer_2
  assign controlled_buffer_1_out = rom_2_data[1] ? adder_2_out : 16'bz;  // Controlled_Buffer controlled_buffer_3
  assign controlled_buffer_1_out = rom_2_data[2] ? {{15{1'b0}}, nor_1_out[0]} : 16'bz;  // Controlled_Buffer controlled_buffer_4
  Register #(.width(16)) R0 (
    .D(controlled_buffer_1_out), .en(and_1_out), .Q({R0_q_4, R0_q_3, R0_q_2, R0_q}), .clk(clock_1_out),
    .clr(Clear));
  Register #(.width(16)) R1 (
    .D(controlled_buffer_1_out), .en(and_2_out), .Q({R1_q_4, R1_q_3, R1_q_2, R1_q}), .clk(clock_1_out),
    .clr(Clear));
  Multiplexer #(.select(4), .width(16)) multiplexer_1 (
    .in0({R0_q_4, R0_q_3, R0_q_2, R0_q}), .in1({R1_q_4, R1_q_3, R1_q_2, R1_q}), .in2(R2_q),
    .in3({R3_q_4, R3_q_3, R3_q_2, R3_q}), .in4({R4_q_3, R4_q_2, R4_q}), .in5({R5_q_3, R5_q_2, R5_q}),
    .in6(R6_q), .in7(R7_q), .in8({16{1'b0}}), .in9({16{1'b0}}), .in10({16{1'b0}}), .in11({16{1'b0}}),
    .in12({16{1'b0}}), .in13({16{1'b0}}), .in14({16{1'b0}}), .in15({16{1'b0}}), .out(multiplexer_1_out),
    .sel({rom_1_data[15], rom_1_data[6:4]}));
  assign not_1_out = ~multiplexer_3_out;  // NOT_Gate not_1, 16 bits wide
  Register #(.width(16)) R2 (.D(controlled_buffer_1_out), .en(and_3_out), .Q(R2_q), .clk(clock_1_out), .clr(Clear));
  Adder #(.width(16)) adder_1 (.a(16'h1), .b(not_1_out), .out(adder_1_out));  // open: cin, cout
  Adder #(.width(16)) adder_2 (.a(multiplexer_2_out), .b(multiplexer_1_out), .out(adder_2_out));  // open: cin, cout
  Register #(.width(16)) R3 (
    .D(controlled_buffer_1_out), .en(and_4_out), .Q({R3_q_4, R3_q_3, R3_q_2, R3_q}), .clk(clock_1_out),
    .clr(Clear));
  Register #(.width(16)) R4 (
    .D(controlled_buffer_1_out), .en(and_5_out), .Q({R4_q_3, R4_q_2, R4_q}), .clk(clock_1_out), .clr(Clear));
  Multiplexer #(.width(16)) multiplexer_2 (
    .in0(adder_1_out), .in1(multiplexer_3_out), .out(multiplexer_2_out), .sel(rom_2_data[0]));
  Register #(.width(16)) R5 (
    .D(controlled_buffer_1_out), .en(and_6_out), .Q({R5_q_3, R5_q_2, R5_q}), .clk(clock_1_out), .clr(Clear));
  Multiplexer #(.select(4), .width(16)) multiplexer_3 (
    .in0({R0_q_4, R0_q_3, R0_q_2, R0_q}), .in1({R1_q_4, R1_q_3, R1_q_2, R1_q}), .in2(R2_q),
    .in3({R3_q_4, R3_q_3, R3_q_2, R3_q}), .in4({R4_q_3, R4_q_2, R4_q}), .in5({R5_q_3, R5_q_2, R5_q}),
    .in6(R6_q), .in7(R7_q), .in8({16{1'b0}}), .in9({16{1'b0}}), .in10({16{1'b0}}), .in11({16{1'b0}}),
    .in12({16{1'b0}}), .in13({16{1'b0}}), .in14({16{1'b0}}), .in15({16{1'b0}}), .out(multiplexer_3_out),
    .sel(rom_1_data[3:0]));
  nor nor_1 (nor_1_out[0], adder_2_out[0], adder_2_out[1], adder_2_out[2], adder_2_out[3], adder_2_out[4], adder_2_out[5], adder_2_out[6], adder_2_out[7], adder_2_out[8], adder_2_out[9], adder_2_out[10], adder_2_out[11], adder_2_out[12], adder_2_out[13], adder_2_out[14], adder_2_out[15]);
  Register #(.width(16)) R6 (.D(controlled_buffer_1_out), .en(and_7_out), .Q(R6_q), .clk(clock_1_out), .clr(Clear));
  Register #(.width(16)) R7 (.D(controlled_buffer_1_out), .en(and_8_out), .Q(R7_q), .clk(clock_1_out), .clr(Clear));
  or or_1 (or_1_out, multiplexer_1_out[0], multiplexer_1_out[1], multiplexer_1_out[2], multiplexer_1_out[3], multiplexer_1_out[4], multiplexer_1_out[5], multiplexer_1_out[6], multiplexer_1_out[7], multiplexer_1_out[8], multiplexer_1_out[9], multiplexer_1_out[10], multiplexer_1_out[11], multiplexer_1_out[12], multiplexer_1_out[13], multiplexer_1_out[14]);
  not not_2 (not_2_out, multiplexer_1_out[15]);
  and and_1 (and_1_out, rom_2_data[9], decoder_1_out0);
  and and_2 (and_2_out, rom_2_data[9], decoder_1_out1);
  and and_3 (and_3_out, rom_2_data[9], decoder_1_out2);
  and and_4 (and_4_out, rom_2_data[9], decoder_1_out3);
  and and_5 (and_5_out, rom_2_data[9], decoder_1_out4);
  and and_6 (and_6_out, rom_2_data[9], decoder_1_out5);
  and and_7 (and_7_out, rom_2_data[9], decoder_1_out6);
  and and_8 (and_8_out, rom_2_data[9], decoder_1_out7);
  and and_9 (and_9_out, or_1_out, not_2_out);
  Decoder #(.select(4)) decoder_1 (
    .out0(decoder_1_out0), .out1(decoder_1_out1), .out2(decoder_1_out2), .out3(decoder_1_out3),
    .out4(decoder_1_out4), .out5(decoder_1_out5), .out6(decoder_1_out6), .out7(decoder_1_out7),
    .sel(rom_1_data_2[11:8]));  // open: out8, out9, out10, out11, out12, out13, out14, out15
  and and_10 (and_10_out, and_9_out, rom_2_data[5]);
  assign controlled_buffer_1_out = rom_2_data[7] ? ram_1_data : 16'bz;  // Controlled_Buffer controlled_buffer_5
  RAM #(.addrWidth(16), .dataWidth(16)) ram_1 (
    .addr(multiplexer_1_out), .data(ram_1_data), .sel(rom_2_data[8]), .clk(clock_1_out), .ld(rom_2_data[7]),
    .clr(CLEAR_2));
  Multiplexer #(.width(16)) multiplexer_4 (
    .in0(16'h1), .in1(multiplexer_3_out), .out(multiplexer_4_out), .sel(and_10_out));
  assign ram_1_data = rom_2_data[6] ? controlled_buffer_1_out : 16'bz;  // Controlled_Buffer controlled_buffer_6
  assign controlled_buffer_1_out = rom_2_data[4] ? {{9{rom_1_data[15]}}, rom_1_data[6:0]} : 16'bz;  // Controlled_Buffer controlled_buffer_7
  Adder #(.width(16)) adder_3 (.a(PC_q), .b(multiplexer_4_out), .out(adder_3_out));  // open: cin, cout
  Register #(.width(16)) PC (.D(adder_3_out), .Q(PC_q), .clk(clock_1_out), .clr(CLEAR_2));  // open: en
  ROM #(.addrWidth(16), .dataWidth(16)) rom_1 (
    .addr(PC_q), .data({rom_1_data_2, rom_1_data[15], rom_1_data[6:0]}));  // open: sel
  Hex_Digit_Display hex_digit_display_33 (.value(PC_q[15:12]));  // open: dp
  Hex_Digit_Display hex_digit_display_34 (.value(PC_q[11:8]));  // open: dp
  Hex_Digit_Display hex_digit_display_35 (.value(PC_q[7:4]));  // open: dp
  Hex_Digit_Display hex_digit_display_36 (.value(PC_q[3:0]));  // open: dp
  ROM #(.addrWidth(4), .dataWidth(16)) rom_2 (.addr(rom_1_data_2[15:12]), .data(rom_2_data));  // open: sel

  // Notes on the sheet:
  //   R7
  //   R6
  //   R5
  //   R4
  //   R3
  //   R2
  //   R1
  //   R0
  //   BUS
  //   MOV
  //   SAD
  //   ADD
  //   SUB
  //   CMP
  //   SA
  //   SA picked
  //   SB picked
  //   2's complement Negation
  //   SB
  //   SA
  //   CMP
  //   SB
  //   >0 Test
  //   Regit Chooser
  //   D
  //   LAD
  //   LIM
  //   SAD
  //   RAM
  //   PROGRAM ROM
  //   8-bit to 16-bit
  //   SB
  //   D
  //   SA
  //   contents of rom_1 (hex, n*v repeats v):
  //   40fc 4100 4303 45ff 4601 1 55 5 3 36 2055 2065 2066 2056 3030 3000 6063 6005 6006 5000 5060 7053
  //   7003 400a 4009 4008 1003 1012 1063 1066
  //   CONTROL ROM
  //   PC OUT
  //   contents of rom_2 (hex, n*v repeats v):
  //   203 204 202 208 210 380 140 20
endmodule
